# Fritzing sketch BlueDruino_Sketch2 (saved by Fritzing 0.8.0b)
breadboards: 1

parts:
  R1 = Resistor [tolerance=±5% resistance=220 package=THT]
  U1 = Bluetooth SMD Module [package=blueradio_br-c40n]  # not connected
  Arduino_UNO = Arduino Uno (Rev3)
  JY-MCU_-_Bluetooth = Bluetooth Mate Silver
  LED1 = LEDs [package=fkit-led-1206]  # not connected
  LED5 = smd LED [color="Yellow (574nm)" package="0603 [SMD]"]
  LED6 = smd LED [color="Red (633nm)" package="0603 [SMD]"]
  LED7 = smd LED [color="Green (555nm)" package="0603 [SMD]"]

nets:
  N1: R1.Pin_0, Arduino_UNO.D1/TX
  N2: R1.Pin_1, JY-MCU_-_Bluetooth.TX_5V
  GND: Arduino_UNO.GND, JY-MCU_-_Bluetooth.GND, LED5.anode, LED6.anode, LED7.anode
  N3: Arduino_UNO.D10_PWM/SS, LED5.cathode
  N4: Arduino_UNO.D11_PWM/MOSI, LED6.cathode
  N5: Arduino_UNO.D12/MISO, LED7.cathode
  N6: Arduino_UNO.D0/RX, JY-MCU_-_Bluetooth.RX_5V
  3V3: Arduino_UNO.3V3, JY-MCU_-_Bluetooth.VCC

notes:
  JY-MCU
  . key
  - vcc
  - gnd
  - txd
  - rxd
  . state
